# Fritzing sketch tmon (saved by Fritzing 0.9.1b)
breadboards: 1

parts:
  R1 = Resistor [tolerance=±5% resistance=220 package=THT]
  LED1 = LED - 5mm [color="Red (633nm)" package="5 mm [THT]"]
  R2 = Resistor [tolerance=±5% resistance=220 package=THT]
  LED2 = LED - 5mm [color="Green (570nm)" package="5 mm [THT]"]
  R3 = Resistor [tolerance=±5% resistance=1k package=THT]
  Raspberry_Pi1 = Raspberry Pi B+
  R4 = Resistor [tolerance=±5% resistance=1k package=THT]
  R5 = Resistor [tolerance=±5% resistance=1k package=THT]
  J1 = Screw terminal - 2 pins [package=THT]
  J2 = Screw terminal - 2 pins [package=THT]
  J3 = Screw terminal - 2 pins [package=THT]
  DS1 = DS18B20 1-Wire Temperature Sensor [part_number=DS18B20]
  R6 = Resistor [tolerance=±5% resistance=220 package=THT]
  R7 = Resistor [tolerance=±5% resistance=220 package=THT]
  R8 = Resistor [tolerance=±5% resistance=560 package=THT]
  U1 = RJ45 Jack [package=rj45-8]
  U2 = RJ45 Jack [package=rj45-8]
  U3 = RJ45 Jack [package=rj45-8]
  LCD1 = LCD screen
  R9 = Resistor [tolerance=±5% resistance=1k package=THT]
  R10 = Resistor [tolerance=±5% resistance=1k package=THT]
  S1 = Pushbutton [package=THT]
  S2 = Pushbutton [package=THT]

nets:
  N1: R1.Pin_0, Raspberry_Pi1.GPIO25
  N2: R1.Pin_1, LED1.anode
  GND: LED1.cathode, LED2.cathode, R3.Pin_1, Raspberry_Pi1.GND, R4.Pin_1, R5.Pin_1, DS1.GND, U1.3, U2.3, U3.3, LCD1.VSS, LCD1.V0, LCD1.R/W, LCD1.LED-, R9.Pin_1, R10.Pin_1
  N3: R2.Pin_0, Raspberry_Pi1.GPIO12
  N4: R2.Pin_1, LED2.anode
  N5: R3.Pin_0, Raspberry_Pi1.GPIO22, J3.pin1
  3V3: Raspberry_Pi1.3v3, Raspberry_Pi1.3V3, DS1.VDD, R6.Pin_1, R7.Pin_1, U1.6, U2.6, U3.6
  N6: Raspberry_Pi1.GPIO4, DS1.DQ, R6.Pin_0, U1.5, U2.5, U3.5
  N7: Raspberry_Pi1.GPIO17, R5.Pin_0, J1.pin1
  N8: Raspberry_Pi1.GPIO27, R4.Pin_0, J2.pin1
  N9: Raspberry_Pi1.GPIO10, R9.Pin_0, S1.leg0
  N10: Raspberry_Pi1.GPIO9, R10.Pin_0, S2.leg0
  N11: Raspberry_Pi1.GPIO7, LCD1.RS
  N12: Raspberry_Pi1.GPIO8, LCD1.E
  N13: Raspberry_Pi1.GPIO23, LCD1.DB4
  N14: Raspberry_Pi1.GPIO18, LCD1.DB5
  N15: Raspberry_Pi1.GPIO15, LCD1.DB6
  N16: Raspberry_Pi1.GPIO14, LCD1.DB7
  5V: Raspberry_Pi1.5V, R8.Pin_0, LCD1.VDD
  N17: J1.pin2, J2.pin2, J3.pin2, R7.Pin_0, S1.leg1, S2.leg1
  N18: R8.Pin_1, LCD1.LED+
